# Fritzing sketch Sprinkler Controller v1.4 (saved by Fritzing 0.8.3b)
circuit board: 10.16cm x 7.62cm
breadboards: 1

parts:
  Raspberry_Pi = Raspberry Pi rev2
  J2 = screw terminal, 10 pins
  SSR8 = SSR 8-DIP [chip_label=IC package="DIP (Dual Inline) [THT]"]
  SSR1 = SSR 8-DIP [chip_label=IC package="DIP (Dual Inline) [THT]"]
  SSR6 = SSR 8-DIP [chip_label=IC package="DIP (Dual Inline) [THT]"]
  SSR5 = SSR 8-DIP [chip_label=IC package="DIP (Dual Inline) [THT]"]
  SSR7 = SSR 8-DIP [chip_label=IC package="DIP (Dual Inline) [THT]"]
  SSR2 = SSR 8-DIP [chip_label=IC package="DIP (Dual Inline) [THT]"]
  SSR9 = SSR 8-DIP [chip_label=IC package="DIP (Dual Inline) [THT]"]
  SSR3 = SSR 8-DIP [chip_label=IC package="DIP (Dual Inline) [THT]"]
  SSR4 = SSR 8-DIP [chip_label=IC package="DIP (Dual Inline) [THT]"]
  SSR10 = SSR 8-DIP [chip_label=IC package="DIP (Dual Inline) [THT]"]
  JP1 = Header 3 [package=screwterminal-3.5mm-3_lock.007s]
  R2 = 100 Ω Resistor [package=THT]
  R1 = 100 Ω Resistor [package=THT]
  J1 = screw terminal, 3 pins

nets:
  N1: Raspberry_Pi.SDA, SSR8.Anode
  N2: Raspberry_Pi.SCL, SSR9.Anode
  N3: Raspberry_Pi.GPIO_7, SSR7.Anode
  N4: Raspberry_Pi.GPIO_0, JP1.1
  N5: Raspberry_Pi.GPIO_1, SSR1.Anode
  N6: Raspberry_Pi.GPIO_2, SSR2.Anode
  N7: Raspberry_Pi.GPIO_3, SSR3.Anode
  N8: Raspberry_Pi.GPIO_4, SSR4.Anode
  N9: Raspberry_Pi.GPIO_5, SSR5.Anode
  N10: Raspberry_Pi.GPIO_6, SSR6.Anode
  N11: Raspberry_Pi.CE0, JP1.3
  N12: Raspberry_Pi.GND, R2.Pin_0, R1.Pin_1
  N13: J2.pin1, SSR1.Output_T2
  N14: J2.pin2, SSR2.Output_T2
  N15: J2.pin3, SSR3.Output_T2
  N16: J2.pin4, SSR4.Output_T2
  N17: J2.pin5, SSR5.Output_T2
  N18: J2.pin6, SSR6.Output_T2
  N19: J2.pin7, SSR7.Output_T2
  N20: J2.pin8, SSR8.Output_T2
  N21: J2.pin9, SSR9.Output_T2
  N22: J2.pin10, SSR10.Output_T2
  N23: SSR8.Cathode, SSR1.Cathode, SSR6.Cathode, SSR5.Cathode, SSR7.Cathode, SSR2.Cathode, SSR9.Cathode, SSR3.Cathode, SSR4.Cathode, R1.Pin_0
  N24: SSR8.Output_T1, SSR1.Output_T1, SSR6.Output_T1, SSR5.Output_T1, SSR7.Output_T1, SSR2.Output_T1, SSR9.Output_T1, SSR3.Output_T1, SSR4.Output_T1, SSR10.Output_T1, J1.pin3
  N25: SSR10.Cathode, R2.Pin_1
  N26: SSR10.Anode, JP1.2
  N27: J1.pin1, J1.pin2

notes:
  Sprinkler Controller v1.4
  Designed by Nick Horvath
  Zones
  24VAC
  1  2  3  4  5  6  7  8  9 10
  Com V+ V-
  Mstr
  Z10

custom parts:
  Raspberry Pi rev2: The awesome Raspberry Pi ARM Board
  SSR 8-DIP: PR29MF11NSZF. With 8 pins on a 300mil dual inline package (DIP) footprint.
  100 Ω Resistor: A generic resistor (0.25W)
